// Logisim project labExperiment1LgiSim.circ as structural Verilog: 1 circuit, main circuit main
module main (
);

  wire and_1_out, carry_out, clock_1_out, clock_2_out, clock_3_out, clock_5_out, clock_6_out, clock_7_out,
       clock_9_out, clock_11_out, clock_13_out, clock_15_out, clock_16_out, nand_1_out, nand_2_out,
       nand_3_out, nand_4_out, nand_5_out, nand_6_out, nand_7_out, nand_8_out, nand_9_out, nand_10_out,
       nand_11_out, nand_12_out, nand_13_out, nand_14_out, nand_15_out, nand_16_out, nand_17_out,
       nand_18_out, nand_19_out, nand_20_out, nand_21_out, nand_22_out, nand_23_out, nand_24_out,
       nand_25_out, nand_26_out, nand_27_out, nand_28_out, nand_29_out, nand_30_out, nand_31_out,
       nand_32_out, nand_33_out, nand_34_out, nand_35_out, nand_36_out, nand_37_out, nand_38_out,
       nand_39_out, nand_41_out, nand_43_out, nand_45_out, nand_46_out, nand_47_out, sum_out, xor_1_out;

  Clock clock_1 (.out(clock_1_out));
  Clock clock_2 (.out(clock_2_out));
  Clock clock_3 (.out(clock_3_out));
  Clock clock_4 (.out(clock_3_out));
  Clock clock_5 (.out(clock_5_out));
  Clock clock_6 (.out(clock_6_out));
  nand nand_1 (nand_1_out, clock_1_out, clock_2_out);
  nand nand_2 (nand_2_out, clock_3_out, clock_3_out);
  xor xor_1 (xor_1_out, clock_5_out, clock_6_out);
  and and_1 (and_1_out, clock_6_out, clock_5_out);
  Clock clock_7 (.out(clock_7_out));
  Clock clock_8 (.out(clock_7_out));
  Clock clock_9 (.out(clock_9_out));
  Clock clock_10 (.out(clock_9_out));
  Clock clock_11 (.out(clock_11_out));
  Clock clock_12 (.out(clock_11_out));
  Clock clock_13 (.out(clock_13_out));
  Clock clock_14 (.out(clock_13_out));
  nand nand_3 (nand_3_out, clock_1_out, nand_1_out);
  nand nand_4 (nand_4_out, nand_1_out, clock_2_out);
  nand nand_5 (nand_5_out, clock_3_out, nand_2_out);
  nand nand_6 (nand_6_out, nand_2_out, clock_3_out);
  nand nand_7 (nand_7_out, clock_11_out, clock_11_out);
  LedBar ledbar_1 (.led0(xor_1_out), .led1(and_1_out));  // open: led2, led3, led4, led5, led6, led7
  nand nand_8 (nand_8_out, clock_7_out, clock_7_out);
  nand nand_9 (nand_9_out, clock_9_out, clock_9_out);
  nand nand_10 (nand_10_out, clock_13_out, clock_13_out);
  nand nand_11 (nand_11_out, nand_3_out, nand_4_out);
  nand nand_12 (nand_12_out, nand_5_out, nand_6_out);
  LED led_1 (.in(nand_11_out));
  LED led_2 (.in(nand_1_out));
  Clock clock_15 (.out(clock_15_out));
  nand nand_13 (nand_13_out, clock_7_out, nand_8_out);
  nand nand_14 (nand_14_out, nand_8_out, clock_7_out);
  nand nand_15 (nand_15_out, clock_9_out, nand_9_out);
  nand nand_16 (nand_16_out, nand_9_out, clock_9_out);
  nand nand_17 (nand_17_out, clock_11_out, nand_7_out);
  nand nand_18 (nand_18_out, nand_7_out, clock_11_out);
  nand nand_19 (nand_19_out, clock_13_out, nand_10_out);
  nand nand_20 (nand_20_out, nand_10_out, clock_13_out);
  nand nand_21 (nand_21_out, nand_12_out, clock_15_out);
  nand nand_22 (nand_22_out, nand_13_out, nand_14_out);
  Clock clock_16 (.out(clock_16_out));
  nand nand_23 (nand_23_out, nand_15_out, nand_16_out);
  nand nand_24 (nand_24_out, nand_17_out, nand_18_out);
  nand nand_25 (nand_25_out, nand_19_out, nand_20_out);
  nand nand_26 (nand_26_out, nand_12_out, nand_21_out);
  nand nand_27 (nand_27_out, nand_21_out, clock_15_out);
  nand nand_28 (nand_28_out, nand_22_out, clock_16_out);
  nand nand_29 (nand_29_out, nand_23_out, nand_37_out);
  nand nand_30 (nand_30_out, nand_24_out, nand_33_out);
  nand nand_31 (nand_31_out, nand_25_out, nand_39_out);
  nand sum (sum_out, nand_26_out, nand_27_out);
  nand carry (carry_out, nand_21_out, nand_2_out);
  nand nand_32 (nand_32_out, nand_24_out, nand_30_out);
  nand nand_33 (nand_33_out, nand_30_out, nand_33_out);
  LED led_3 (.in(sum_out));
  LED led_4 (.in(carry_out));
  nand nand_34 (nand_34_out, nand_22_out, nand_28_out);
  nand nand_35 (nand_35_out, nand_28_out, clock_16_out);
  nand nand_36 (nand_36_out, nand_23_out, nand_29_out);
  nand nand_37 (nand_37_out, nand_29_out, nand_37_out);
  nand nand_38 (nand_38_out, nand_25_out, nand_31_out);
  nand nand_39 (nand_39_out, nand_31_out, nand_39_out);
  // Digital_Oscilloscope digital_oscilloscope_1: pin names not known; wires that end beside it: sum_out, carry_out
  // Digital_Oscilloscope digital_oscilloscope_2: pin names not known; wires that end beside it: clock_3_out, clock_3_out, clock_15_out
  nand nand_40 (nand_37_out, nand_34_out, nand_35_out);
  LED led_5 (.in(nand_37_out));
  nand nand_41 (nand_41_out, nand_28_out, nand_8_out);
  LED led_6 (.in(nand_41_out));
  nand nand_42 (nand_33_out, nand_36_out, nand_37_out);
  LED led_7 (.in(nand_33_out));
  nand nand_43 (nand_43_out, nand_29_out, nand_9_out);
  LED led_8 (.in(nand_43_out));
  nand nand_44 (nand_39_out, nand_32_out, nand_33_out);
  LED led_9 (.in(nand_39_out));
  nand nand_45 (nand_45_out, nand_30_out, nand_7_out);
  LED led_10 (.in(nand_45_out));
  nand nand_46 (nand_46_out, nand_38_out, nand_39_out);
  LED led_11 (.in(nand_46_out));
  nand nand_47 (nand_47_out, nand_31_out, nand_10_out);
  LED led_12 (.in(nand_47_out));
  LedBar ledbar_2 (
    .led3(nand_47_out), .led4(nand_45_out), .led5(nand_43_out), .led6(nand_41_out), .led7(nand_46_out));  // open: led0, led1, led2
  // Digital_Oscilloscope digital_oscilloscope_3: pin names not known; wires that end beside it: nand_41_out, clock_7_out, nand_45_out, nand_47_out
endmodule
