// Logisim project labExperiment6LogiSim.circ as structural Verilog: 1 circuit, main circuit main
module main (
  input  [1:0] in_1,
  input  [3:0] in_2,
  input  [3:0] in_3,
  input  [3:0] in_4,
  input  [3:0] in_5
);

  wire clock_1_out, multiplexer_1_out, multiplexer_2_out, multiplexer_3_out, multiplexer_4_out;
  wire [3:0] register_1_q, register_2_q, register_3_q, register_4_q;

  Clock clock_1 (.out(clock_1_out));
  Register #(.width(4)) register_1 (.D(in_2), .en(1'b1), .clk(clock_1_out), .Q(register_1_q));  // open: clr
  Register #(.width(4)) register_2 (.D(in_3), .en(1'b1), .clk(clock_1_out), .Q(register_2_q));  // open: clr
  Register #(.width(4)) register_3 (.D(in_4), .en(1'b1), .clk(clock_1_out), .Q(register_3_q));  // open: clr
  Register #(.width(4)) register_4 (.D(in_5), .en(1'b1), .clk(clock_1_out), .Q(register_4_q));  // open: clr
  Multiplexer #(.select(2)) multiplexer_1 (
    .in0(register_1_q[0]), .in1(register_2_q[0]), .in2(register_3_q[0]), .in3(register_4_q[0]),
    .out(multiplexer_1_out), .sel(in_1));
  Multiplexer #(.select(2)) multiplexer_2 (
    .in0(register_1_q[1]), .in1(register_2_q[1]), .in2(register_3_q[1]), .in3(register_4_q[1]),
    .out(multiplexer_2_out), .sel(in_1));
  Multiplexer #(.select(2)) multiplexer_3 (
    .in0(register_1_q[2]), .in1(register_2_q[2]), .in2(register_3_q[2]), .in3(register_4_q[2]),
    .out(multiplexer_3_out), .sel(in_1));
  Multiplexer #(.select(2)) multiplexer_4 (
    .in0(register_1_q[3]), .in1(register_2_q[3]), .in2(register_3_q[3]), .in3(register_4_q[3]),
    .out(multiplexer_4_out), .sel(in_1));
  LedBar #(.matrixcols(4)) ledbar_1 (
    .led0(multiplexer_4_out), .led1(multiplexer_3_out), .led2(multiplexer_2_out), .led3(multiplexer_1_out));
endmodule
